# Fritzing sketch Tumbglove (saved by Fritzing 0.7.11b)
breadboards: 1

parts:
  Arduino1 = Arduino
  R2 = Resistor [tolerance=±5% resistance=10k package=THT]
  R1 = Basic Flex Resistor
  IC1 = SO08 [chip_label=KXM52-1050 package=SO]
  J1 = Basic Force Sensing Resistor (FSR) [package=THT]
  R3 = Resistor [tolerance=±5% resistance=10k package=THT]

nets (from the breadboard view):
  N1: Arduino1.+5V, R1.Pin_2, IC1.1, IC1.2, J1.pin_1
  N2: Arduino1.GND, R2.Pin_0, IC1.3, IC1.4, R3.Pin_1
  N3: Arduino1.A0, R2.Pin_1, R1.pin_1
  N4: Arduino1.A1, J1.pin_0, R3.Pin_0
  N5: Arduino1.A2, IC1.6
  N6: Arduino1.A3, IC1.7
  N7: Arduino1.A4, IC1.8

notes:
  ARDUINO
  LEONARDO
  +Y Z Y X
  ↑ 8 7 6
  → +X
  Reblogged Sensor
  Pager Sensor
  Liked Sensor
